# Fritzing sketch breadboard (saved by Fritzing 0.9.4)
breadboards: 1

parts:
  Part1 = SPI OLED Monochrome 128x64 0.96 inch
  Part2 = Arduino Nano (Rev3.0)
  S1 = Momentary Switch [package=ksa_sealed_tac_switch]
  Part3 = ENC28J60 Breakout Board

nets:
  GND: Part1.GND, Part2.GND, S1.1, Part3.GND
  VDD: Part1.VDD, Part2.5V, Part3.VCC
  N1: Part1.SCK, Part2.D7
  N2: Part1.SDA, Part2.D9
  N3: Part1.RES, Part2.D6
  N4: Part1.DC, Part2.D5
  N5: Part1.CS, Part2.D4
  N6: Part2.RESET, S1.3
  N7: Part2.D10, Part3.CS
  N8: Part2.D11/MOSI, Part3.SI
  N9: Part2.D12/MISO, Part3.SO
  N10: Part2.D13/SCK, Part3.SCK

custom parts:
  SPI OLED Monochrome 128x64 0.96 inch: Unknown 128x64 0.96 inch 128x64 SPI Monochrome OLED display
  ENC28J60 Breakout Board: This is a breakout board for the Microchip ENC28J60 stand-alone ethernet controller. The ENC28J60 has an SPI interface. It operates at 3.3 Volts.
